// Logisim project cpuwu.circ as structural Verilog: 1 circuit, main circuit main
module main (
  output Imm1,
  output Imm2,
  output [7:0] NextPC,
  output Write,
  output [7:0] instr,
  output [2:0] WriteReg,
  output [7:0] PrintOut,
  output [7:0] RegData1,
  output [7:0] ALU1,
  output Print,
  output [7:0] MemAdr,
  output Cjmp,
  output MemW,
  output [7:0] MemOut,
  output [7:0] RegData2,
  output [7:0] MemWrite,
  output [7:0] ALUout,
  output [7:0] RegDataW,
  output MemR,
  output [2:0] ReadReg1,
  output [2:0] ReadReg2,
  output [7:0] JumpAdr,
  output Jump,
  output [2:0] Oper,
  output [7:0] Compare,
  output EqZero,
  output Zero
);

  wire and_1_out, and_2_out, and_3_out, and_4_out, and_5_out, and_6_out, and_7_out, and_8_out,
       decoder_1_out0, decoder_1_out1, decoder_1_out2, decoder_1_out3, decoder_1_out4, decoder_1_out5,
       decoder_1_out6, decoder_1_out7, not_2_out, SysClocl_out;
  wire [7:0] adder_2_out, and_9_out, divider_1_out, multiplexer_8_out, multiplier_1_out, not_1_out, or_1_out,
       PC_q, subtractor_1_out, u0_q, u1_q, u2_q, u3_q, u4_q, u5_q, u6_q, u7_q, xor_1_out;
  wire [23:0] ram_1_dout;

  Clock SysClocl (.out(SysClocl_out));
  Multiplexer #(.width(8)) multiplexer_1 (.in0(NextPC), .in1(ALU1), .out(instr), .sel(Cjmp));
  Multiplexer multiplexer_2 (.in0(Jump), .in1(EqZero), .out(Cjmp), .sel(Zero));
  Register PC (.D(instr), .en(1'b1), .clk(SysClocl_out), .Q(PC_q));  // open: clr
  Comparator #(.mode("unsigned")) comparator_1 (.a(Compare), .b({8{1'b0}}), .eq(EqZero));  // open: gt, lt
  Adder adder_1 (.a(8'h1), .b(PC_q), .out(NextPC));  // open: cin, cout
  RAM #(.dataWidth(32), .enables("line")) ram_1 (
    .addr(PC_q), .we(1'b0), .clk(SysClocl_out),
    .dout({Write, WriteReg, Imm1, ReadReg1, ram_1_dout[23:19], Imm2, ReadReg2, ram_1_dout[14:10], Oper, MemR, MemW, Print, Jump, Zero, ram_1_dout[1:0]}));  // open: din
  Decoder #(.select(3)) decoder_1 (
    .out0(decoder_1_out0), .out1(decoder_1_out1), .out2(decoder_1_out2), .out3(decoder_1_out3),
    .out4(decoder_1_out4), .out5(decoder_1_out5), .out6(decoder_1_out6), .out7(decoder_1_out7), .sel(WriteReg));  // open: en
  Register u0 (.D(RegDataW), .en(and_1_out), .clk(SysClocl_out), .Q(u0_q));  // open: clr
  and and_1 (and_1_out, decoder_1_out0, Write);
  Register u1 (.D(RegDataW), .en(and_2_out), .clk(SysClocl_out), .Q(u1_q));  // open: clr
  and and_2 (and_2_out, decoder_1_out1, Write);
  Register u2 (.D(RegDataW), .en(and_3_out), .clk(SysClocl_out), .Q(u2_q));  // open: clr
  and and_3 (and_3_out, decoder_1_out2, Write);
  Register u3 (.D(RegDataW), .en(and_4_out), .clk(SysClocl_out), .Q(u3_q));  // open: clr
  and and_4 (and_4_out, decoder_1_out3, Write);
  Register u4 (.D(RegDataW), .en(and_5_out), .clk(SysClocl_out), .Q(u4_q));  // open: clr
  and and_5 (and_5_out, decoder_1_out4, Write);
  Register u5 (.D(RegDataW), .en(and_6_out), .clk(SysClocl_out), .Q(u5_q));  // open: clr
  and and_6 (and_6_out, decoder_1_out5, Write);
  Register u6 (.D(RegDataW), .en(and_7_out), .clk(SysClocl_out), .Q(u6_q));  // open: clr
  and and_7 (and_7_out, decoder_1_out6, Write);
  Register u7 (.D(RegDataW), .en(and_8_out), .clk(SysClocl_out), .Q(u7_q));  // open: clr
  and and_8 (and_8_out, decoder_1_out7, Write);
  Multiplexer #(.select(3), .width(8)) multiplexer_3 (
    .in0(u0_q), .in1(u1_q), .in2(u2_q), .in3(u3_q), .in4(u4_q), .in5(u5_q), .in6(u6_q), .in7(u7_q),
    .out(RegData1), .sel(ReadReg1));
  Multiplexer #(.select(3), .width(8)) multiplexer_4 (
    .in0(u0_q), .in1(u1_q), .in2(u2_q), .in3(u3_q), .in4(u4_q), .in5(u5_q), .in6(u6_q), .in7(u7_q),
    .out(MemWrite), .sel(ReadReg2));
  Multiplexer #(.width(8)) multiplexer_5 (.in0(RegData1), .in1({ReadReg1, ram_1_dout[23:19]}), .out(ALU1), .sel(Imm1));
  Multiplexer #(.width(8)) multiplexer_6 (
    .in0(MemWrite), .in1({ReadReg2, ram_1_dout[14:10]}), .out(Compare), .sel(Imm2));
  Adder adder_2 (.a(ALU1), .b(Compare), .out(adder_2_out));  // open: cin, cout
  Subtractor subtractor_1 (.a(ALU1), .b(Compare), .out(subtractor_1_out));  // open: bin, bout
  Multiplier multiplier_1 (.a(ALU1), .b(Compare), .out(multiplier_1_out));  // open: cin, cout
  Divider divider_1 (.a(ALU1), .b(Compare), .out(divider_1_out));  // open: upper, rem
  assign and_9_out = ALU1 & Compare;  // AND_Gate and_9, 8 bits wide
  assign or_1_out = ALU1 | Compare;  // OR_Gate or_1, 8 bits wide
  assign not_1_out = ~ALU1;  // NOT_Gate not_1, 8 bits wide
  assign xor_1_out = ALU1 ^ Compare;  // XOR_Gate xor_1, 8 bits wide
  Multiplexer #(.width(8)) multiplexer_7 (.in0(ALUout), .in1(MemOut), .out(RegDataW), .sel(MemR));
  Register register_1 (.D(multiplexer_8_out), .en(1'b1), .clk(SysClocl_out), .Q(PrintOut));  // open: clr
  Multiplexer #(.width(8)) multiplexer_8 (.in1(ALU1), .out(multiplexer_8_out), .sel(Print));  // open: in0
  Multiplexer #(.select(3), .width(8)) multiplexer_9 (
    .in0(adder_2_out), .in1(subtractor_1_out), .in2(multiplier_1_out), .in3(divider_1_out), .in4(and_9_out),
    .in5(or_1_out), .in6(not_1_out), .in7(xor_1_out), .out(ALUout), .sel(Oper));
  not not_2 (not_2_out, SysClocl_out);
  RAM #(.enables("line")) ram_2 (.addr(ALU1), .we(MemW), .clk(not_2_out), .din(MemWrite), .dout(MemOut));
  _7_Segment_Display u_7_segment_display_1 ();  // open: g, f, a, b, e, d, c, dp
  // BCD_to_7_Segment_decoder bcd_to_7_segment_decoder_1: pin names not known
  _7_Segment_Display u_7_segment_display_2 ();  // open: g, f, a, b, e, d, c, dp
  // BCD_to_7_Segment_decoder bcd_to_7_segment_decoder_2: pin names not known
  // Binary_to_BCD_converter #(.binvalue(8)) binary_to_bcd_converter_1: pin names not known; wires that end beside it: PrintOut
  _7_Segment_Display u_7_segment_display_3 ();  // open: g, f, a, b, e, d, c, dp
  // BCD_to_7_Segment_decoder bcd_to_7_segment_decoder_3: pin names not known
  Hex_Digit_Display hex_digit_display_1 (.value(PrintOut[7:4]));  // open: dp
  Hex_Digit_Display hex_digit_display_2 (.value(PrintOut[3:0]));  // open: dp

  assign JumpAdr = ALU1;
  assign MemAdr = ALU1;
  assign RegData2 = MemWrite;

  // Notes on the sheet:
  //   John Graham & Emma Hodor
  //   I pledge my honor that I have abided by the Stevens Honor System.
  //   Instruction Memory
  //   CPuwu
  //   0d
  //   0x
endmodule
